# Fritzing sketch mainboard (saved by Fritzing 0.9.10b)
circuit board: 6.75539cm x 5.40956cm

parts:
  Part1 = Adafruit 4-channel I2C-safe Bi-directional Logic Level Converter [part_number="Adafruit #757"]
  Part2 = Adafruit Metro M0 Express
  QTPy = Adafruit QT Py [part_number="Adafruit #4600"]
  J1 = female pin header, 3 pins [form="♀ (female)"]
  R1 = Resistor [tolerance=±5% resistance=100 power=0.25 package=THT]
  J2 = female pin header, 3 pins [form="♀ (female)"]
  J3 = female pin header, 3 pins [form="♀ (female)"]
  J4 = female pin header, 9 pins [form="♀ (female)"]
  J6 = female pin header, 2 pins [form="♀ (female)"]
  R2 = Resistor [tolerance=±5% power=0.25 resistance=4700 package=THT]
  R3 = Resistor [tolerance=±5% power=0.25 resistance=10000 package=THT]
  J5 = female pin header, 4 pins [form="♀ (female)"]

nets (from the pcb view):
  N1: Part1.A4, QTPy.A3
  N2: Part1.A3, Part2.D12
  N3: Part1.A2, Part2.D13
  N4: Part1.B4, R1.Pin_0
  N5: Part1.B3, J3.pin1
  N6: Part1.B2, J2.pin1
  N7: Part1.HV, Part2.+5V, J1.pin2, J2.pin2, J3.pin2
  N8: Part2.A1, R3.Pin_1
  N9: Part2.MISO, J4.pin4
  N10: Part2.SCK, J4.pin3
  GND: Part2.GND, QTPy.GND, J1.pin3, J2.pin3, J3.pin3, J4.pin2, R2.Pin_1, J5.pin2
  N11: Part2.D11, QTPy.TX
  N12: Part2.D10, QTPy.RX
  N13: Part2.D9, J4.pin9
  N14: Part2.D8, J4.pin8
  N15: Part2.D7, J4.pin7
  N16: Part2.D6, J4.pin6
  N17: Part2.D5, J5.pin1
  N18: Part2.D4, J5.pin3
  N19: J1.pin1, R1.Pin_1
  N20: J6.pin1, R3.Pin_0

notes:
  Power input to Metro is by barrel connector 7.2v center positive;
  note on board bottom, +V is on pad farthewst from "front" of connector;
  xx
  G
  +V
  Vbat for ADC
  10k
  1 k
  divides to 0.091
  7.4v in = 0.67v out)
  (11.1 in = 1.09v out)
  Steering Servo PWM
  (Wht header)
  TX Serial to camera
  GND
  RX Serial from camera
  +5v
  (Blu header)
  ESC PWM
  (Grn header)
  NeoPixel Strip
  (Yellow header)
  ---------------TFT-----------------------
  5v G CK MI MO TC RST DC CC
  RD BK BU GE BN GY OR YE WH

custom parts:
  Adafruit 4-channel I2C-safe Bi-directional Logic Level Converter: Because the Arduino (and Basic Stamp) are 5V devices, and most modern sensors, displays, flash cards and modes are 3.3V-only, many makers find that they need to perform level shifting/conversion to protect the 3.3V device from 5V. We do have some other handy level shifters in the shop, from the DIP 74LVC245 to the fancy bi-directional TXB0108. However, neither of these are happy to work with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
  Adafruit Metro M0 Express: Metro is our series of microcontroller boards for use with the Arduino IDE. This new Metro board looks a whole lot like our original Metro 328, but with a huge upgrade. Instead of the ATmega328, this Metro features a ATSAMD21G18 chip, an ARM Cortex M0+. It's our first Metro that is designed for use with CircuitPython! CircuitPython is our beginner-oriented flavor of MicroPython - and as the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
  Adafruit QT Py: What a cutie pie! Or is it... a QT Py? This diminutive dev board comes with our favorite lil chip, the SAMD21 (as made famous in our GEMMA M0 and Trinket M0 boards). This time it comes with our favorite connector - the STEMMA QT, a chainable I2C port that can be used with any of our STEMMA QT sensors and accessories. OLEDs! Inertial Measurment Units! Sensors a-plenty. All plug-and-play thanks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
